# Fritzing sketch Smart Controller (saved by Fritzing 1.0.2b)
breadboards: 1

parts:
  A1 = Particle - Photon2
  HC-SR04_Sensor_1 = HC-SR04 Ultrasonic Distance Sensor
  OLED_I2C1 = OLED 128x64 I2C Monochrome Display
  M1 = BMP280
  U1 = ENCODER_RGB [package=encoder_led_2]

nets:
  GND: A1.Pin_4, A1.Pin_30, A1.Pin_35, HC-SR04_Sensor_1.GND, OLED_I2C1.GND, M1.GND
  N1: A1.Pin_13, HC-SR04_Sensor_1.TRIG
  N2: A1.Pin_14, HC-SR04_Sensor_1.ECHO
  N3: A1.Pin_17, OLED_I2C1.SDA, M1.SDA
  N4: A1.Pin_18, OLED_I2C1.SCK, M1.SCL
  N5: A1.Pin_19, U1.R
  N6: A1.Pin_20, U1.G
  N7: A1.Pin_21, U1.SW
  N8: A1.Pin_22, U1.B
  N9: A1.Pin_26, HC-SR04_Sensor_1.VCC, U1.+
  VDD: OLED_I2C1.VDD, M1.VIN

custom parts:
  Particle - Photon2: The Photon 2 is a microcontroller and Wi-Fi networking developed by particle. Features: 802.11a/b/g/n Wi-Fi, 2.4 GHz and 5 GHz Integrated PCB antenna Integrated U.FL connector for external antenna Integrated RF switch BLE 5 using same antenna as Wi-Fi Realtek RTL8721DM MCU ARM Cortex M33 CPU, 200 MHz 2048 KB (2 MB) user application maximum size 3072 KB (3 MB) of RAM available to user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
  BMP280: Temperature Humidity Barometric presure Sensor, I2C
  ENCODER_RGB: SparkFun RGB rotary Encoder
